# Fritzing sketch Schematic (saved by Fritzing 1.0.5)
breadboards: 1

parts:
  Part1 = Arduino Uno (Rev3)
  PIR1 = PIR sensor
  J1 = Basic Servo
  Mod1 = KY-004 Key Switch Module [package="Breakout board"]
  OLED_I2C1 = OLED 128x64 I2C Monochrome Display
  Mod2 = Passive Buzzer
  Mod3 = KY-016 RGB Full Color LED Module [package="Breakout board"]
  Mod4 = KY-018 Photoresistor Module [package="Breakout board"]

nets:
  N1: Part1.A0, Mod4.S
  N2: Part1.A4/SDA, OLED_I2C1.SDA
  N3: Part1.A5/SCL, OLED_I2C1.SCK
  N4: Part1.D8, Mod2.S
  N5: Part1.D10_PWM/SS, J1.pulse
  N6: Part1.D11_PWM/MOSI, Mod3.G
  N7: Part1.D12/MISO, Mod3.R
  N8: Part1.D2, PIR1.SIG
  N9: Part1.D3_PWM, Mod1.S
  VDD: Part1.5V, PIR1.VDD, J1.vcc, OLED_I2C1.VDD, Mod4.Vin
  GND: Part1.GND, PIR1.GND, J1.gnd, Mod1.-, OLED_I2C1.GND, Mod2.-, Mod3.-, Mod4.-

custom parts:
  KY-004 Key Switch Module: Arduino Key Switch Module Keyes KY-004 is a push button that will output a high signal when pressed.
  KY-016 RGB Full Color LED Module: KY-016 Arduino full color 5mm RGB LED, different colors can be obtained by mixing the three primary colors.
  KY-018 Photoresistor Module: KY-018 Photoresistor module, used to measure light intensity. It can determine the presence or absence of light.
